// Logisim project Clackertron_sync.circ as structural Verilog: 18 circuits, main circuit main
module main (
  input  in_1,
  input  in_2,
  input  in_3,
  input  A,
  input  B,
  input  CI,
  output S,
  output CO
);

  wire half_add_2_c, half_add_2_s, half_add_3_c, single_read_latch_1_q, spdt_co_1_c1;

  D_Flip_Flop d_ff_1 ();  // open: D, clk, Q, Qn, preset, reset
  D_Latch d_latch_1 ();  // open: CLK, EN, D, Q, nQ
  D_Register d_register_1 ();  // open: D, CLK, EN_ovd, EN_pg, Q, nQ, FB
  LED led_1 (.in(spdt_co_1_c1));
  SPDT_CO spdt_co_1 (
    .coil_L(in_2), .coil_R(1'b0), .CLK(in_1), .NO1(single_read_latch_1_q), .C1(spdt_co_1_c1));  // open: NC1
  single_read_latch single_read_latch_1 (
    .D(in_3), .OE(in_2), .CLK(in_1), .FB(single_read_latch_1_q), .Q(single_read_latch_1_q));
  Half_Add half_add_1 ();  // open: CLK, A, B, C, S, nS
  Full_Add full_add_1 ();  // open: B, nB, A, CLK, CI, S, CO
  ADD add_1 ();  // open: CLK, CI, A, B, nB, S, CO
  Half_Add half_add_2 (.A(A), .B(B), .C(half_add_2_c), .S(half_add_2_s));  // open: CLK, nS
  MUX mux_1 ();  // open: S, CLK, A, B, out_5
  DEMUX demux_1 ();  // open: in_1, S, CLK, A, B
  D_Register d_register_2 ();  // open: D, CLK, EN_ovd, EN_pg, Q, nQ, FB
  INC inc_1 ();  // open: A, nA, CLK, S, nS, nCO
  INC_PC inc_pc_1 ();  // open: CLK, nPCH, PCH, nPCL, PCL, INCH, INCL
  Half_Add half_add_3 (.A(half_add_2_s), .B(CI), .C(half_add_3_c), .S(S));  // open: CLK, nS
  or or_1 (CO, half_add_3_c, half_add_2_c);
  INC_DEC inc_dec_1 ();  // open: CLK, D, IE, DEC, OE, S, CO
  ADD_SUB add_sub_1 ();  // open: CLK, A, nA, B, nB, CI, s_SUB, s_ADD, S, CO, OA
  LU lu_1 ();  // open: CI, CLK, B, nB, A, nA, s_mode, S, CO

  // Notes on the sheet:
  //   FA old
endmodule

module single_read_latch (
  input  D,
  input  OE,
  input  CLK,
  input  FB,
  output Q
);

  wire and_1_out, hiz_detector_1_out_2, not_1_out, t_ff_1_q, t_ff_2_q;

  HiZ_Detector hiz_detector_1 (.in_1(FB), .out_2(hiz_detector_1_out_2));
  not not_1 (not_1_out, OE);
  T_Flip_Flop #(.trigger("falling")) t_ff_1 (
    .T(1'b1), .clk(and_1_out), .Q(t_ff_1_q), .reset(not_1_out));  // open: Qn, preset
  and and_1 (and_1_out, CLK, ~hiz_detector_1_out_2);  // AND_Gate
  T_Flip_Flop #(.trigger("falling")) t_ff_2 (
    .T(1'b1), .clk(t_ff_1_q), .Q(t_ff_2_q), .reset(not_1_out));  // open: Qn, preset
  D_Flip_Flop #(.trigger("low")) d_ff_1 (.D(D), .clk(OE), .Q(Q), .reset(t_ff_2_q));  // open: Qn, preset

  // Notes on the sheet:
  //   OE high -> enables "current flow" of Capacitor
  //   FB  HiZ  -> halts "current flow" of Capacitor
  //   Capacitor emulation as a delay unit
endmodule

module double_read_latch (
  input  D,
  input  OE,
  input  CLK,
  input  FB,
  output Q
);

  wire and_1_out, hiz_detector_1_out_2, not_1_out, t_ff_1_q, t_ff_2_q, t_ff_3_q;

  HiZ_Detector hiz_detector_1 (.in_1(FB), .out_2(hiz_detector_1_out_2));
  not not_1 (not_1_out, OE);
  T_Flip_Flop #(.trigger("falling")) t_ff_1 (
    .T(1'b1), .clk(and_1_out), .Q(t_ff_1_q), .reset(not_1_out));  // open: Qn, preset
  and and_1 (and_1_out, CLK, ~hiz_detector_1_out_2);  // AND_Gate
  T_Flip_Flop #(.trigger("falling")) t_ff_2 (
    .T(1'b1), .clk(t_ff_1_q), .Q(t_ff_2_q), .reset(not_1_out));  // open: Qn, preset
  T_Flip_Flop #(.trigger("falling")) t_ff_3 (
    .T(1'b1), .clk(t_ff_2_q), .Q(t_ff_3_q), .reset(not_1_out));  // open: Qn, preset
  D_Flip_Flop #(.trigger("low")) d_ff_1 (.D(D), .clk(OE), .Q(Q), .reset(t_ff_3_q));  // open: Qn, preset

  // Notes on the sheet:
  //   OE high -> enables "current flow" of Capacitor
  //   FB  HiZ  -> halts "current flow" of Capacitor
  //   Capacitor emulation as a delay unit
endmodule

module single_read_latch_8 (
  input  [7:0] D,
  input  CLK,
  input  OE,
  input  FB,
  output [7:0] Q
);

  single_read_latch single_read_latch_1 (.D(D[0]), .OE(OE), .CLK(CLK), .FB(FB), .Q(Q[0]));
  single_read_latch single_read_latch_2 (.D(D[1]), .OE(OE), .CLK(CLK), .FB(FB), .Q(Q[1]));
  single_read_latch single_read_latch_3 (.D(D[2]), .OE(OE), .CLK(CLK), .FB(FB), .Q(Q[2]));
  single_read_latch single_read_latch_4 (.D(D[3]), .OE(OE), .CLK(CLK), .FB(FB), .Q(Q[3]));
  single_read_latch single_read_latch_5 (.D(D[4]), .OE(OE), .CLK(CLK), .FB(FB), .Q(Q[4]));
  single_read_latch single_read_latch_6 (.D(D[5]), .OE(OE), .CLK(CLK), .FB(FB), .Q(Q[5]));
  single_read_latch single_read_latch_7 (.D(D[6]), .OE(OE), .CLK(CLK), .FB(FB), .Q(Q[6]));
  single_read_latch single_read_latch_8 (.D(D[7]), .OE(OE), .CLK(CLK), .FB(FB), .Q(Q[7]));
endmodule

module D_Latch (
  input  CLK,
  input  EN,
  input  D,
  output Q,
  output nQ
);

  wire and_1_out, spdt_ci_1_no1;

  SPDT_CI spdt_ci_1 (.coil_L(EN), .coil_R(1'b0), .CLK(CLK), .C1(D), .NO1(spdt_ci_1_no1));  // open: NC1
  D_Flip_Flop d_ff_1 (.D(spdt_ci_1_no1), .clk(and_1_out), .Q(Q), .Qn(nQ));  // open: preset, reset
  and and_1 (and_1_out, CLK, EN);

  // Notes on the sheet:
  //   max CLK = 2
endmodule

module D_Register (
  input  [7:0] D,
  input  CLK,
  input  EN_ovd,
  input  EN_pg,
  output [7:0] Q,
  output [7:0] nQ,
  output FB
);

  wire and_1_out, or_1_out, single_read_latch_1_q, spdt_co_1_c1, undriven;
  wire [7:0] mux_1_out_5;

  single_read_latch single_read_latch_1 (.D(1'b1), .OE(EN_pg), .CLK(CLK), .FB(FB), .Q(single_read_latch_1_q));
  SPDT_CO spdt_co_1 (
    .coil_L(1'b0), .coil_R(EN_pg), .CLK(CLK), .NC1(1'b0), .NO1(single_read_latch_1_q), .C1(spdt_co_1_c1));
  Pull_Resistor pull_resistor_1 (.node(spdt_co_1_c1));
  MUX mux_1 (.S(or_1_out), .CLK(CLK), .B(D), .out_5(mux_1_out_5));  // open: A
  or or_1 (or_1_out, EN_ovd, spdt_co_1_c1);
  D_Flip_Flop d_ff_1 (.D(mux_1_out_5[0]), .clk(and_1_out), .Q(Q[0]), .Qn(nQ[0]));  // open: preset, reset
  D_Flip_Flop d_ff_2 (.D(mux_1_out_5[1]), .clk(and_1_out), .Q(Q[1]), .Qn(nQ[1]));  // open: preset, reset
  D_Flip_Flop d_ff_3 (.D(mux_1_out_5[2]), .clk(and_1_out), .Q(Q[2]), .Qn(nQ[2]));  // open: preset, reset
  D_Flip_Flop d_ff_4 (.D(mux_1_out_5[3]), .clk(and_1_out), .Q(Q[3]), .Qn(nQ[3]));  // open: preset, reset
  D_Flip_Flop d_ff_5 (.D(mux_1_out_5[4]), .clk(and_1_out), .Q(Q[4]), .Qn(nQ[4]));  // open: preset, reset
  D_Flip_Flop d_ff_6 (.D(mux_1_out_5[5]), .clk(and_1_out), .Q(Q[5]), .Qn(nQ[5]));  // open: preset, reset
  D_Flip_Flop d_ff_7 (.D(mux_1_out_5[6]), .clk(and_1_out), .Q(Q[6]), .Qn(nQ[6]));  // open: preset, reset
  D_Flip_Flop d_ff_8 (.D(mux_1_out_5[7]), .clk(and_1_out), .Q(Q[7]), .Qn(nQ[7]));  // open: preset, reset
  and and_1 (and_1_out, CLK, or_1_out);
  SPDT_CO spdt_co_2 (.coil_L(or_1_out), .coil_R(1'b0), .CLK(CLK), .NC1(undriven), .NO1(1'b1), .C1(FB));
  // NoConnect on undriven

  // Notes on the sheet:
  //   max CLK = 2
  //   feed back signal for "current" based devices
  //   is non HiZ iff D is directly connected to the D-Latches
endmodule

module Half_Add (
  input  CLK,
  input  A,
  input  B,
  output S,
  output nS,
  output C
);

  DPDT_CICO dpdt_cico_1 (.coil_L(A), .coil_R(B), .CLK(CLK), .C1(1'b1), .NC2(B), .NO2(1'b0), .C2(C), .NC1(nS), .NO1(S));

  // Notes on the sheet:
  //   Half Adder Relay equivalent
endmodule

module Full_Add (
  input  B,
  input  nB,
  input  A,
  input  CI,
  input  CLK,
  output S,
  output CO
);

  DPDT_COCO dpdt_coco_1 (.coil_L(CI), .coil_R(A), .CLK(CLK), .NC1(A), .NO1(B), .NC2(B), .NO2(nB), .C1(CO), .C2(S));
endmodule

module ADD (
  input  CLK,
  input  CI,
  input  [7:0] A,
  input  [7:0] B,
  input  [7:0] nB,
  output [7:0] S,
  output CO
);

  wire full_add_1_co, full_add_2_co, full_add_3_co, full_add_4_co, full_add_5_co, full_add_6_co,
       full_add_7_co;

  Full_Add full_add_1 (.B(B[0]), .nB(nB[0]), .A(A[0]), .CLK(CLK), .CI(CI), .S(S[0]), .CO(full_add_1_co));
  Full_Add full_add_2 (.B(B[1]), .nB(nB[1]), .A(A[1]), .CLK(CLK), .CI(full_add_1_co), .S(S[1]), .CO(full_add_2_co));
  Full_Add full_add_3 (.B(B[2]), .nB(nB[2]), .A(A[2]), .CLK(CLK), .CI(full_add_2_co), .S(S[2]), .CO(full_add_3_co));
  Full_Add full_add_4 (.B(B[3]), .nB(nB[3]), .A(A[3]), .CLK(CLK), .CI(full_add_3_co), .S(S[3]), .CO(full_add_4_co));
  Full_Add full_add_5 (.B(B[4]), .nB(nB[4]), .A(A[4]), .CLK(CLK), .CI(full_add_4_co), .S(S[4]), .CO(full_add_5_co));
  Full_Add full_add_6 (.B(B[5]), .nB(nB[5]), .A(A[5]), .CLK(CLK), .CI(full_add_5_co), .S(S[5]), .CO(full_add_6_co));
  Full_Add full_add_7 (.B(B[6]), .nB(nB[6]), .A(A[6]), .CLK(CLK), .CI(full_add_6_co), .S(S[6]), .CO(full_add_7_co));
  Full_Add full_add_8 (.B(B[7]), .nB(nB[7]), .A(A[7]), .CLK(CLK), .CI(full_add_7_co), .S(S[7]), .CO(CO));

  // Notes on the sheet:
  //   max CLK = 8
endmodule

module ADD_SUB (
  input  CLK,
  input  [7:0] A,
  input  [7:0] nA,
  input  [7:0] B,
  input  [7:0] nB,
  input  CI,
  input  s_SUB,
  input  s_ADD,
  output [7:0] S,
  output CO,
  output OA
);

  wire add_1_co;
  wire [7:0] mux_1_out_5;

  MUX mux_1 (.S(s_SUB), .CLK(CLK), .A(A), .B(nA), .out_5(mux_1_out_5));
  ADD add_1 (.CLK(CLK), .CI(CI), .A(mux_1_out_5), .B(B), .nB(nB), .S(S), .CO(add_1_co));
  SPDT_CO spdt_co_1 (.coil_L(add_1_co), .coil_R(1'b0), .CLK(CLK), .NC1(s_SUB), .NO1(s_ADD), .C1(CO));
  or or_1 (OA, s_SUB, s_ADD);

  // Notes on the sheet:
  //   Relay logic invalid for ~SUB & ~ADD
  //   Output Available
endmodule

module MUX (
  input  [7:0] A,
  input  S,
  input  CLK,
  input  [7:0] B,
  output [7:0] out_5
);

  DPDT_COCO dpdt_coco_1 (
    .coil_L(S), .coil_R(1'b0), .CLK(CLK), .NC1(A[0]), .NO1(B[0]), .NC2(A[1]), .NO2(B[1]), .C1(out_5[0]),
    .C2(out_5[1]));
  DPDT_COCO dpdt_coco_2 (
    .coil_L(S), .coil_R(1'b0), .CLK(CLK), .NC1(A[2]), .NO1(B[2]), .NC2(A[3]), .NO2(B[3]), .C1(out_5[2]),
    .C2(out_5[3]));
  DPDT_COCO dpdt_coco_3 (
    .coil_L(S), .coil_R(1'b0), .CLK(CLK), .NC1(A[4]), .NO1(B[4]), .NC2(A[5]), .NO2(B[5]), .C1(out_5[4]),
    .C2(out_5[5]));
  DPDT_COCO dpdt_coco_4 (
    .coil_L(S), .coil_R(1'b0), .CLK(CLK), .NC1(A[6]), .NO1(B[6]), .NC2(A[7]), .NO2(B[7]), .C1(out_5[6]),
    .C2(out_5[7]));
endmodule

module DEMUX (
  input  [7:0] in_1,
  input  S,
  input  CLK,
  output [7:0] A,
  output [7:0] B
);

  DPDT_CICI dpdt_cici_1 (
    .coil_L(S), .coil_R(1'b0), .CLK(CLK), .C1(in_1[0]), .C2(in_1[1]), .NC1(A[0]), .NO1(B[0]), .NC2(A[1]),
    .NO2(B[1]));
  DPDT_CICI dpdt_cici_2 (
    .coil_L(S), .coil_R(1'b0), .CLK(CLK), .C1(in_1[2]), .C2(in_1[3]), .NC1(A[2]), .NO1(B[2]), .NC2(A[3]),
    .NO2(B[3]));
  DPDT_CICI dpdt_cici_3 (
    .coil_L(S), .coil_R(1'b0), .CLK(CLK), .C1(in_1[4]), .C2(in_1[5]), .NC1(A[4]), .NO1(B[4]), .NC2(A[5]),
    .NO2(B[5]));
  DPDT_CICI dpdt_cici_4 (
    .coil_L(S), .coil_R(1'b0), .CLK(CLK), .C1(in_1[6]), .C2(in_1[7]), .NC1(A[6]), .NO1(B[6]), .NC2(A[7]),
    .NO2(B[7]));
endmodule

module INC (
  input  CLK,
  input  [7:0] A,
  input  [7:0] nA,
  output nCO,
  output [7:0] S,
  output [7:0] nS
);

  wire buffer_1_out, buffer_2_out, buffer_3_out, buffer_4_out, buffer_5_out, buffer_6_out, buffer_7_out,
       buffer_8_out, buffer_9_out, buffer_10_out, buffer_11_out, buffer_12_out, buffer_13_out, buffer_14_out,
       buffer_15_out, buffer_16_out, buffer_17_out, buffer_18_out, buffer_19_out, buffer_20_out,
       buffer_21_out, buffer_22_out, buffer_23_out, buffer_24_out, buffer_25_out, buffer_26_out,
       buffer_27_out, buffer_28_out, or_1_out, or_2_out, or_3_out, or_4_out, or_5_out, or_6_out;

  DPDT_COCO dpdt_coco_1 (
    .coil_L(nA[0]), .coil_R(1'b0), .CLK(CLK), .NC1(nA[1]), .NO1(A[1]), .NC2(A[1]), .NO2(nA[1]), .C1(S[1]),
    .C2(nS[1]));
  DPDT_COCO dpdt_coco_2 (
    .coil_L(or_1_out), .coil_R(1'b0), .CLK(CLK), .NC1(nA[2]), .NO1(A[2]), .NC2(A[2]), .NO2(nA[2]), .C1(S[2]),
    .C2(nS[2]));
  DPDT_COCO dpdt_coco_3 (
    .coil_L(or_2_out), .coil_R(1'b0), .CLK(CLK), .NC1(nA[3]), .NO1(A[3]), .NC2(A[3]), .NO2(nA[3]), .C1(S[3]),
    .C2(nS[3]));
  DPDT_COCO dpdt_coco_4 (
    .coil_L(or_3_out), .coil_R(1'b0), .CLK(CLK), .NC1(nA[4]), .NO1(A[4]), .NC2(A[4]), .NO2(nA[4]), .C1(S[4]),
    .C2(nS[4]));
  DPDT_COCO dpdt_coco_5 (
    .coil_L(or_4_out), .coil_R(1'b0), .CLK(CLK), .NC1(nA[5]), .NO1(A[5]), .NC2(A[5]), .NO2(nA[5]), .C1(S[5]),
    .C2(nS[5]));
  DPDT_COCO dpdt_coco_6 (
    .coil_L(or_5_out), .coil_R(1'b0), .CLK(CLK), .NC1(nA[6]), .NO1(A[6]), .NC2(A[6]), .NO2(nA[6]), .C1(S[6]),
    .C2(nS[6]));
  DPDT_COCO dpdt_coco_7 (
    .coil_L(or_6_out), .coil_R(1'b0), .CLK(CLK), .NC1(nA[7]), .NO1(A[7]), .NC2(A[7]), .NO2(nA[7]), .C1(S[7]),
    .C2(nS[7]));
  or or_1 (or_1_out, buffer_1_out, buffer_2_out);
  or or_2 (or_2_out, buffer_3_out, buffer_4_out, buffer_5_out);
  or or_3 (or_3_out, buffer_6_out, buffer_7_out, buffer_8_out, buffer_9_out);
  or or_4 (or_4_out, buffer_10_out, buffer_11_out, buffer_12_out, buffer_13_out, buffer_14_out);
  or or_5 (or_5_out, buffer_15_out, buffer_16_out, buffer_17_out, buffer_18_out, buffer_19_out, buffer_20_out);
  or or_6 (or_6_out, buffer_21_out, buffer_22_out, buffer_23_out, buffer_24_out, buffer_25_out, buffer_26_out, buffer_27_out);
  buf buffer_1 (buffer_1_out, nA[0]);
  buf buffer_2 (buffer_2_out, nA[1]);
  buf buffer_3 (buffer_3_out, nA[0]);
  buf buffer_4 (buffer_4_out, nA[1]);
  buf buffer_5 (buffer_5_out, nA[2]);
  buf buffer_6 (buffer_6_out, nA[0]);
  buf buffer_7 (buffer_7_out, nA[1]);
  buf buffer_8 (buffer_8_out, nA[2]);
  buf buffer_9 (buffer_9_out, nA[3]);
  buf buffer_10 (buffer_10_out, nA[0]);
  buf buffer_11 (buffer_11_out, nA[1]);
  buf buffer_12 (buffer_12_out, nA[2]);
  buf buffer_13 (buffer_13_out, nA[3]);
  buf buffer_14 (buffer_14_out, nA[4]);
  buf buffer_15 (buffer_15_out, nA[0]);
  buf buffer_16 (buffer_16_out, nA[1]);
  buf buffer_17 (buffer_17_out, nA[2]);
  buf buffer_18 (buffer_18_out, nA[3]);
  buf buffer_19 (buffer_19_out, nA[4]);
  buf buffer_20 (buffer_20_out, nA[5]);
  buf buffer_21 (buffer_21_out, nA[0]);
  buf buffer_22 (buffer_22_out, nA[1]);
  buf buffer_23 (buffer_23_out, nA[2]);
  buf buffer_24 (buffer_24_out, nA[3]);
  buf buffer_25 (buffer_25_out, nA[4]);
  buf buffer_26 (buffer_26_out, nA[5]);
  buf buffer_27 (buffer_27_out, nA[6]);
  buf buffer_28 (buffer_28_out, or_6_out);
  or or_7 (nCO, buffer_28_out, nA[7]);

  assign nS[0] = A[0];
  assign S[0] = nA[0];

  // Notes on the sheet:
  //   max CLK = 1
endmodule

module INC_DEC (
  input  CLK,
  input  [7:0] D,
  input  IE,
  input  DEC,
  input  OE,
  output [7:0] S,
  output CO
);

  wire inc_1_nco;
  wire [7:0] d_register_1_nq, d_register_1_q, inc_1_ns, inc_1_s, mux_1_out_5, mux_2_out_5, mux_3_out_5;

  D_Register d_register_1 (.D(D), .CLK(CLK), .EN_ovd(IE), .Q(d_register_1_q), .nQ(d_register_1_nq));  // open: EN_pg, FB
  MUX mux_1 (.S(DEC), .CLK(CLK), .A(d_register_1_q), .B(d_register_1_nq), .out_5(mux_1_out_5));
  MUX mux_2 (.S(DEC), .CLK(CLK), .A(d_register_1_nq), .B(d_register_1_q), .out_5(mux_2_out_5));
  INC inc_1 (.A(mux_1_out_5), .nA(mux_2_out_5), .CLK(CLK), .S(inc_1_s), .nS(inc_1_ns), .nCO(inc_1_nco));
  MUX mux_3 (.S(DEC), .CLK(CLK), .A(inc_1_s), .B(inc_1_ns), .out_5(mux_3_out_5));
  SPDT_CI spdt_ci_1 (.coil_L(inc_1_nco), .coil_R(1'b0), .CLK(CLK), .C1(OE), .NC1(CO));  // open: NO1
  MUX mux_4 (.S(OE), .CLK(CLK), .B(mux_3_out_5), .out_5(S));  // open: A

  // Notes on the sheet:
  //   output must not directly feedback input
endmodule

module INC_PC (
  input  CLK,
  input  [7:0] nPCL,
  input  [7:0] PCL,
  input  [7:0] nPCH,
  input  [7:0] PCH,
  output [7:0] INCL,
  output [7:0] INCH
);

  wire buffer_1_out, buffer_2_out, buffer_3_out, buffer_4_out, buffer_5_out, buffer_6_out, buffer_7_out,
       buffer_8_out, buffer_9_out, buffer_10_out, buffer_11_out, buffer_12_out, buffer_13_out, buffer_14_out,
       buffer_15_out, buffer_16_out, buffer_17_out, buffer_18_out, buffer_19_out, buffer_20_out,
       buffer_21_out, buffer_22_out, buffer_23_out, buffer_24_out, buffer_25_out, buffer_26_out,
       buffer_27_out, buffer_28_out, buffer_29_out, buffer_30_out, buffer_31_out, buffer_32_out,
       buffer_33_out, buffer_34_out, buffer_35_out, buffer_36_out, buffer_37_out, buffer_38_out,
       buffer_39_out, buffer_40_out, buffer_41_out, buffer_42_out, buffer_43_out, buffer_44_out,
       buffer_45_out, buffer_46_out, buffer_47_out, buffer_48_out, buffer_49_out, buffer_50_out,
       buffer_51_out, buffer_52_out, buffer_53_out, buffer_54_out, buffer_55_out, buffer_56_out,
       buffer_57_out, buffer_58_out, buffer_59_out, buffer_60_out, buffer_61_out, buffer_62_out, or_1_out,
       or_2_out, or_3_out, or_4_out, or_5_out, or_6_out, or_7_out, or_8_out, or_9_out, or_10_out, or_11_out,
       or_12_out, or_13_out, or_14_out, spdt_co_16_c1, undriven;

  SPDT_CO spdt_co_1 (.coil_L(nPCL[0]), .coil_R(1'b0), .CLK(CLK), .NC1(nPCL[1]), .NO1(PCL[1]), .C1(INCL[1]));
  SPDT_CO spdt_co_2 (.coil_L(or_1_out), .coil_R(1'b0), .CLK(CLK), .NC1(nPCL[2]), .NO1(PCL[2]), .C1(INCL[2]));
  SPDT_CO spdt_co_3 (.coil_L(or_2_out), .coil_R(1'b0), .CLK(CLK), .NC1(nPCL[3]), .NO1(PCL[3]), .C1(INCL[3]));
  SPDT_CO spdt_co_4 (.coil_L(or_3_out), .coil_R(1'b0), .CLK(CLK), .NC1(nPCL[4]), .NO1(PCL[4]), .C1(INCL[4]));
  SPDT_CO spdt_co_5 (.coil_L(or_4_out), .coil_R(1'b0), .CLK(CLK), .NC1(nPCL[5]), .NO1(PCL[5]), .C1(INCL[5]));
  SPDT_CO spdt_co_6 (.coil_L(or_5_out), .coil_R(1'b0), .CLK(CLK), .NC1(nPCL[6]), .NO1(PCL[6]), .C1(INCL[6]));
  SPDT_CO spdt_co_7 (.coil_L(or_6_out), .coil_R(1'b0), .CLK(CLK), .NC1(nPCL[7]), .NO1(PCL[7]), .C1(INCL[7]));
  SPDT_CO spdt_co_8 (.coil_L(spdt_co_16_c1), .coil_R(1'b0), .CLK(CLK), .NC1(nPCH[0]), .NO1(PCH[0]), .C1(INCH[0]));
  SPDT_CO spdt_co_9 (.coil_L(or_8_out), .coil_R(1'b0), .CLK(CLK), .NC1(nPCH[1]), .NO1(PCH[1]), .C1(INCH[1]));
  SPDT_CO spdt_co_10 (.coil_L(or_9_out), .coil_R(1'b0), .CLK(CLK), .NC1(nPCH[2]), .NO1(PCH[2]), .C1(INCH[2]));
  SPDT_CO spdt_co_11 (.coil_L(or_10_out), .coil_R(1'b0), .CLK(CLK), .NC1(nPCH[3]), .NO1(PCH[3]), .C1(INCH[3]));
  SPDT_CO spdt_co_12 (.coil_L(or_11_out), .coil_R(1'b0), .CLK(CLK), .NC1(nPCH[4]), .NO1(PCH[4]), .C1(INCH[4]));
  SPDT_CO spdt_co_13 (.coil_L(or_12_out), .coil_R(1'b0), .CLK(CLK), .NC1(nPCH[5]), .NO1(PCH[5]), .C1(INCH[5]));
  SPDT_CO spdt_co_14 (.coil_L(or_13_out), .coil_R(1'b0), .CLK(CLK), .NC1(nPCH[6]), .NO1(PCH[6]), .C1(INCH[6]));
  SPDT_CO spdt_co_15 (.coil_L(or_14_out), .coil_R(1'b0), .CLK(CLK), .NC1(nPCH[7]), .NO1(PCH[7]), .C1(INCH[7]));
  or or_1 (or_1_out, buffer_46_out, buffer_47_out);
  or or_2 (or_2_out, buffer_48_out, buffer_1_out, buffer_49_out);
  buf buffer_1 (buffer_1_out, nPCL[1]);
  buf buffer_2 (buffer_2_out, nPCL[1]);
  or or_3 (or_3_out, buffer_50_out, buffer_2_out, buffer_51_out, buffer_3_out);
  buf buffer_3 (buffer_3_out, nPCL[3]);
  buf buffer_4 (buffer_4_out, nPCL[1]);
  or or_4 (or_4_out, buffer_52_out, buffer_4_out, buffer_53_out, buffer_5_out, buffer_54_out);
  buf buffer_5 (buffer_5_out, nPCL[3]);
  buf buffer_6 (buffer_6_out, nPCL[1]);
  or or_5 (or_5_out, buffer_55_out, buffer_6_out, buffer_56_out, buffer_57_out, buffer_7_out, buffer_58_out);
  buf buffer_7 (buffer_7_out, nPCL[4]);
  buf buffer_8 (buffer_8_out, nPCL[1]);
  or or_6 (or_6_out, buffer_59_out, buffer_8_out, buffer_60_out, buffer_9_out, buffer_61_out, buffer_10_out, buffer_62_out);
  buf buffer_9 (buffer_9_out, nPCL[3]);
  buf buffer_10 (buffer_10_out, nPCL[5]);
  or or_7 (or_7_out, or_6_out, nPCL[7]);
  buf buffer_11 (buffer_11_out, spdt_co_16_c1);
  or or_8 (or_8_out, buffer_11_out, buffer_12_out);
  buf buffer_12 (buffer_12_out, nPCH[0]);
  buf buffer_13 (buffer_13_out, spdt_co_16_c1);
  or or_9 (or_9_out, buffer_13_out, buffer_14_out, buffer_15_out);
  buf buffer_14 (buffer_14_out, nPCH[0]);
  buf buffer_15 (buffer_15_out, nPCH[1]);
  buf buffer_16 (buffer_16_out, spdt_co_16_c1);
  buf buffer_17 (buffer_17_out, nPCH[0]);
  or or_10 (or_10_out, buffer_16_out, buffer_17_out, buffer_18_out, buffer_19_out);
  buf buffer_18 (buffer_18_out, nPCH[1]);
  buf buffer_19 (buffer_19_out, nPCH[2]);
  buf buffer_20 (buffer_20_out, spdt_co_16_c1);
  buf buffer_21 (buffer_21_out, nPCH[0]);
  or or_11 (or_11_out, buffer_20_out, buffer_21_out, buffer_22_out, buffer_23_out, buffer_24_out);
  buf buffer_22 (buffer_22_out, nPCH[1]);
  buf buffer_23 (buffer_23_out, nPCH[2]);
  buf buffer_24 (buffer_24_out, nPCH[3]);
  buf buffer_25 (buffer_25_out, spdt_co_16_c1);
  buf buffer_26 (buffer_26_out, nPCH[0]);
  buf buffer_27 (buffer_27_out, nPCH[1]);
  or or_12 (or_12_out, buffer_25_out, buffer_26_out, buffer_27_out, buffer_28_out, buffer_29_out, buffer_30_out);
  buf buffer_28 (buffer_28_out, nPCH[2]);
  buf buffer_29 (buffer_29_out, nPCH[3]);
  buf buffer_30 (buffer_30_out, nPCH[4]);
  buf buffer_31 (buffer_31_out, spdt_co_16_c1);
  buf buffer_32 (buffer_32_out, nPCH[0]);
  buf buffer_33 (buffer_33_out, nPCH[1]);
  or or_13 (or_13_out, buffer_31_out, buffer_32_out, buffer_33_out, buffer_34_out, buffer_35_out, buffer_36_out, buffer_37_out);
  buf buffer_34 (buffer_34_out, nPCH[2]);
  buf buffer_35 (buffer_35_out, nPCH[3]);
  buf buffer_36 (buffer_36_out, nPCH[4]);
  buf buffer_37 (buffer_37_out, nPCH[5]);
  buf buffer_38 (buffer_38_out, spdt_co_16_c1);
  buf buffer_39 (buffer_39_out, nPCH[0]);
  buf buffer_40 (buffer_40_out, nPCH[1]);
  buf buffer_41 (buffer_41_out, nPCH[2]);
  or or_14 (or_14_out, buffer_38_out, buffer_39_out, buffer_40_out, buffer_41_out, buffer_42_out, buffer_43_out, buffer_44_out, buffer_45_out);
  buf buffer_42 (buffer_42_out, nPCH[3]);
  buf buffer_43 (buffer_43_out, nPCH[4]);
  buf buffer_44 (buffer_44_out, nPCH[5]);
  buf buffer_45 (buffer_45_out, nPCH[6]);
  buf buffer_46 (buffer_46_out, nPCL[0]);
  buf buffer_47 (buffer_47_out, nPCL[1]);
  buf buffer_48 (buffer_48_out, nPCL[0]);
  buf buffer_49 (buffer_49_out, nPCL[2]);
  buf buffer_50 (buffer_50_out, nPCL[0]);
  buf buffer_51 (buffer_51_out, nPCL[2]);
  buf buffer_52 (buffer_52_out, nPCL[0]);
  buf buffer_53 (buffer_53_out, nPCL[2]);
  buf buffer_54 (buffer_54_out, nPCL[4]);
  buf buffer_55 (buffer_55_out, nPCL[0]);
  buf buffer_56 (buffer_56_out, nPCL[2]);
  buf buffer_57 (buffer_57_out, nPCL[3]);
  buf buffer_58 (buffer_58_out, nPCL[5]);
  buf buffer_59 (buffer_59_out, nPCL[0]);
  buf buffer_60 (buffer_60_out, nPCL[2]);
  buf buffer_61 (buffer_61_out, nPCL[4]);
  buf buffer_62 (buffer_62_out, nPCL[6]);
  // NoConnect on undriven
  SPDT_CO spdt_co_16 (.coil_L(1'b0), .coil_R(or_7_out), .CLK(CLK), .NC1(undriven), .NO1(1'b1), .C1(spdt_co_16_c1));
  Pull_Resistor pull_resistor_1 (.node(spdt_co_16_c1));

  assign INCL[0] = nPCL[0];

  // Notes on the sheet:
  //   Pull down MUST NOT be used in real design
endmodule

module XOR_8 (
  input  [7:0] B,
  input  [7:0] nB,
  input  [7:0] A,
  input  CLK,
  output [7:0] S
);

  SPDT_CO spdt_co_1 (.coil_L(1'b0), .coil_R(A[0]), .CLK(CLK), .NC1(B[0]), .NO1(nB[0]), .C1(S[0]));
  SPDT_CO spdt_co_2 (.coil_L(1'b0), .coil_R(A[1]), .CLK(CLK), .NC1(B[1]), .NO1(nB[1]), .C1(S[1]));
  SPDT_CO spdt_co_3 (.coil_L(1'b0), .coil_R(A[2]), .CLK(CLK), .NC1(B[2]), .NO1(nB[2]), .C1(S[2]));
  SPDT_CO spdt_co_4 (.coil_L(1'b0), .coil_R(A[3]), .CLK(CLK), .NC1(B[3]), .NO1(nB[3]), .C1(S[3]));
  SPDT_CO spdt_co_5 (.coil_L(1'b0), .coil_R(A[4]), .CLK(CLK), .NC1(B[4]), .NO1(nB[4]), .C1(S[4]));
  SPDT_CO spdt_co_6 (.coil_L(1'b0), .coil_R(A[5]), .CLK(CLK), .NC1(B[5]), .NO1(nB[5]), .C1(S[5]));
  SPDT_CO spdt_co_7 (.coil_L(1'b0), .coil_R(A[6]), .CLK(CLK), .NC1(B[6]), .NO1(nB[6]), .C1(S[6]));
  SPDT_CO spdt_co_8 (.coil_L(1'b0), .coil_R(A[7]), .CLK(CLK), .NC1(B[7]), .NO1(nB[7]), .C1(S[7]));
endmodule

module LU (
  input  CLK,
  input  [2:0] s_mode,
  input  [7:0] B,
  input  [7:0] nB,
  input  [7:0] A,
  input  [7:0] nA,
  input  CI,
  output [7:0] S,
  output CO
);

  wire [0:0] spdt_co_1_c1;
  wire [7:0] and_1_out, mux_1_out_5, mux_2_out_5, mux_3_out_5, mux_4_out_5, or_1_out, xor_8_1_s;

  SPDT_CO spdt_co_1 (.coil_L(1'b0), .coil_R(s_mode[1]), .CLK(CLK), .NO1(CI), .C1(spdt_co_1_c1[0]));  // open: NC1
  assign or_1_out = A | B;  // OR_Gate or_1, 8 bits wide
  assign and_1_out = A & B;  // AND_Gate and_1, 8 bits wide
  XOR_8 xor_8_1 (.CLK(CLK), .B(B), .nB(nB), .A(A), .S(xor_8_1_s));
  MUX mux_1 (.S(s_mode[0]), .CLK(CLK), .A(or_1_out), .B(and_1_out), .out_5(mux_1_out_5));
  MUX mux_2 (.S(s_mode[0]), .CLK(CLK), .A(xor_8_1_s), .B(nA), .out_5(mux_2_out_5));
  MUX mux_3 (
    .S(s_mode[0]), .CLK(CLK), .A({A[6:0], spdt_co_1_c1[0]}), .B({spdt_co_1_c1[0], A[7:1]}),
    .out_5(mux_3_out_5));
  MUX mux_4 (.S(s_mode[1]), .CLK(CLK), .A(mux_1_out_5), .B(mux_2_out_5), .out_5(mux_4_out_5));
  SPDT_CO spdt_co_2 (.coil_L(1'b0), .coil_R(s_mode[0]), .CLK(CLK), .NC1(A[7]), .NO1(A[0]), .C1(CO));
  MUX mux_5 (.S(s_mode[2]), .CLK(CLK), .A(mux_4_out_5), .B(mux_3_out_5), .out_5(S));

  // Other names for the same wires on the sheet: m0 = s_mode[0]; m1 = s_mode[1]; m2 = s_mode[2]

  // Notes on the sheet:
  //   ASL: C <- X <- 0
  //   LSR: 0 -> X -> C
  //   ROL: C <- X <- C
  //   ROR: C -> X -> C
  //   Mux Table - s_mode:
  //   000 -> OR
  //   001 -> AND
  //   010 -> EOR
  //   011 -> NEG
  //   1Rr -- R=Rotate - r=Right:
  //   100 -> ASL
  //   101 -> LSR
  //   110 -> ROL
  //   111 -> ROR
  //   ROL/ASL
  //   ROR/LSR
endmodule

module PC (
  input  [7:0] AD_BUS_I,
  input  [7:0] D_BUS_I,
  input  s_BUS_SEL,
  input  CI,
  input  s_inc,
  input  s_in,
  input  s_out,
  input  CLK,
  output [7:0] AD_BUS_O,
  output [7:0] D_BUS_O,
  output CO
);

  wire d_register_1_fb;
  wire [3:0] inc_1_p1, inc_1_p1_2, inc_1_p4, inc_1_p4_2, mux_2_out_5, mux_2_out_5_2;
  wire [7:0] demux_1_b, mux_1_out_5, single_read_latch_8_1_q;

  MUX mux_1 (.S(s_BUS_SEL), .CLK(CLK), .A(AD_BUS_I), .B(D_BUS_I), .out_5(mux_1_out_5));
  Hex_Digit_Display #(.decimalPoint("false")) hex_digit_display_1 (.value(inc_1_p4_2));
  Hex_Digit_Display #(.decimalPoint("false")) hex_digit_display_2 (.value(inc_1_p4));
  // INC inc_1: pin names not known; wires that end beside it: {inc_1_p1_2, inc_1_p1}, CI, CLK, {inc_1_p4_2, inc_1_p4}, CO
  single_read_latch_8 single_read_latch_8_1 (
    .D({inc_1_p4_2, inc_1_p4}), .CLK(CLK), .OE(s_inc), .FB(d_register_1_fb), .Q(single_read_latch_8_1_q));
  Hex_Digit_Display #(.decimalPoint("false")) hex_digit_display_3 (.value(mux_2_out_5_2));
  MUX mux_2 (.S(s_inc), .CLK(CLK), .A(mux_1_out_5), .B(single_read_latch_8_1_q), .out_5({mux_2_out_5_2, mux_2_out_5}));
  Hex_Digit_Display #(.decimalPoint("false")) hex_digit_display_4 (.value(mux_2_out_5));
  Hex_Digit_Display #(.decimalPoint("false")) hex_digit_display_5 (.value(inc_1_p1_2));
  D_Register d_register_1 (
    .D({mux_2_out_5_2, mux_2_out_5}), .CLK(CLK), .EN_ovd(s_in), .EN_pg(s_inc), .Q({inc_1_p1_2, inc_1_p1}),
    .FB(d_register_1_fb));  // open: nQ
  Hex_Digit_Display #(.decimalPoint("false")) hex_digit_display_6 (.value(inc_1_p1));
  DEMUX demux_1 (.in_1({inc_1_p1_2, inc_1_p1}), .S(s_out), .CLK(CLK), .B(demux_1_b));  // open: A
  DEMUX demux_2 (.in_1(demux_1_b), .S(s_BUS_SEL), .CLK(CLK), .A(AD_BUS_O), .B(D_BUS_O));

  // Other names for the same wires on the sheet: bs = s_BUS_SEL; c = CLK
endmodule
