// Logisim project Demo_Full_Adder_Logic.circ as structural Verilog: 1 circuit, main circuit main
module main (
  input  A,
  input  B,
  input  C
);

  wire and_1_out, and_2_out, and_3_out, and_4_out, and_5_out, and_6_out, and_7_out, and_8_out, and_9_out,
       and_10_out, and_11_out, and_12_out, not_1_out, not_2_out, not_3_out, or_1_out, or_2_out, or_3_out,
       or_4_out, or_5_out, or_6_out, xor_1_out, xor_2_out, xor_3_out;

  not not_1 (not_1_out, B);
  not not_2 (not_2_out, B);
  xor xor_1 (xor_1_out, A, B);
  and and_1 (and_1_out, A, B);
  not not_3 (not_3_out, C);
  and and_2 (and_2_out, xor_1_out, C);
  and and_3 (and_3_out, not_1_out, A);
  or or_1 (or_1_out, and_3_out, and_4_out);
  and and_4 (and_4_out, ~A, B);  // AND_Gate
  and and_5 (and_5_out, A, B);
  xor xor_2 (xor_2_out, A, C);
  // Probe on xor_3_out
  xor xor_3 (xor_3_out, xor_1_out, C);
  // Probe on or_2_out
  or or_2 (or_2_out, and_2_out, and_1_out);
  and and_6 (and_6_out, not_3_out, or_1_out);
  and and_7 (and_7_out, ~or_1_out, C);  // AND_Gate
  and and_8 (and_8_out, or_1_out, C);
  and and_9 (and_9_out, not_2_out, xor_2_out);
  or or_3 (or_3_out, and_9_out, and_10_out);
  and and_10 (and_10_out, ~xor_2_out, B);  // AND_Gate
  and and_11 (and_11_out, B, xor_2_out);
  or or_4 (or_4_out, and_11_out, and_12_out);
  and and_12 (and_12_out, ~xor_2_out, C);  // AND_Gate
  // Probe on or_5_out
  or or_5 (or_5_out, and_6_out, and_7_out);
  // Probe on or_6_out
  or or_6 (or_6_out, and_8_out, and_5_out);
  // Probe on or_3_out
  // Probe on or_4_out

  // Notes on the sheet:
  //   Dual Relay Logic
  //   Single Relay Logic
  //   Generic Logic
endmodule
