// Logisim project Relay_sync.circ as structural Verilog: 8 circuits, main circuit SPDT_CI
module HiZ_Detector (
  input  in_1,
  output out_2
);

  wire buffer_1_out, buffer_2_out;

  buf buffer_1 (buffer_1_out, in_1);
  buf buffer_2 (buffer_2_out, in_1);
  Pull_Resistor #(.pull(1)) pull_resistor_1 (.node(buffer_1_out));
  Pull_Resistor pull_resistor_2 (.node(buffer_2_out));
  xor xor_1 (out_2, buffer_1_out, buffer_2_out);
endmodule

module SPDT_CI (
  input  C1,
  input  coil_L,
  input  coil_R,
  input  CLK,
  output NC1,
  output NO1
);

  wire controlled_buffer_1_out, d_ff_1_q, demultiplexer_1_out0, demultiplexer_1_out1, hiz_detector_1_out_2,
       hiz_detector_2_out_2, nor_1_out, xnor_1_out, xor_1_out;

  HiZ_Detector hiz_detector_1 (.in_1(coil_L), .out_2(hiz_detector_1_out_2));
  nor nor_1 (nor_1_out, hiz_detector_1_out_2, hiz_detector_2_out_2);
  HiZ_Detector hiz_detector_2 (.in_1(coil_R), .out_2(hiz_detector_2_out_2));
  xor xor_1 (xor_1_out, coil_L, coil_R);
  assign controlled_buffer_1_out = nor_1_out ? xor_1_out : 1'bz;  // Controlled_Buffer controlled_buffer_1
  Pull_Resistor pull_resistor_1 (.node(controlled_buffer_1_out));
  D_Flip_Flop d_ff_1 (.D(controlled_buffer_1_out), .clk(CLK), .Q(d_ff_1_q));  // open: Qn, preset, reset
  xnor xnor_1 (xnor_1_out, controlled_buffer_1_out, d_ff_1_q);
  Demultiplexer #(.tristate("true")) demultiplexer_1 (
    .out0(demultiplexer_1_out0), .out1(demultiplexer_1_out1), .in(C1), .sel(controlled_buffer_1_out));
  assign NC1 = xnor_1_out ? demultiplexer_1_out0 : 1'bz;  // Controlled_Buffer controlled_buffer_2
  assign NO1 = xnor_1_out ? demultiplexer_1_out1 : 1'bz;  // Controlled_Buffer controlled_buffer_3
endmodule

module SPDT_CO (
  input  NC1,
  input  NO1,
  input  coil_L,
  input  coil_R,
  input  CLK,
  output C1
);

  wire controlled_buffer_1_out, d_ff_1_q, hiz_detector_1_out_2, hiz_detector_2_out_2, multiplexer_1_out,
       nor_1_out, xnor_1_out, xor_1_out;

  HiZ_Detector hiz_detector_1 (.in_1(coil_L), .out_2(hiz_detector_1_out_2));
  nor nor_1 (nor_1_out, hiz_detector_1_out_2, hiz_detector_2_out_2);
  HiZ_Detector hiz_detector_2 (.in_1(coil_R), .out_2(hiz_detector_2_out_2));
  xor xor_1 (xor_1_out, coil_L, coil_R);
  assign controlled_buffer_1_out = nor_1_out ? xor_1_out : 1'bz;  // Controlled_Buffer controlled_buffer_1
  Pull_Resistor pull_resistor_1 (.node(controlled_buffer_1_out));
  D_Flip_Flop d_ff_1 (.D(controlled_buffer_1_out), .clk(CLK), .Q(d_ff_1_q));  // open: Qn, preset, reset
  assign C1 = xnor_1_out ? multiplexer_1_out : 1'bz;  // Controlled_Buffer controlled_buffer_2
  xnor xnor_1 (xnor_1_out, controlled_buffer_1_out, d_ff_1_q);
  Multiplexer multiplexer_1 (.in0(NC1), .in1(NO1), .out(multiplexer_1_out), .sel(controlled_buffer_1_out));
endmodule

module DPDT_CICI (
  input  C1,
  input  coil_L,
  input  coil_R,
  input  CLK,
  input  C2,
  output NC1,
  output NO1,
  output NC2,
  output NO2
);

  wire controlled_buffer_1_out, d_ff_1_q, demultiplexer_1_out0, demultiplexer_1_out1, demultiplexer_2_out0,
       demultiplexer_2_out1, hiz_detector_1_out_2, hiz_detector_2_out_2, nor_1_out, xnor_1_out, xor_1_out;

  HiZ_Detector hiz_detector_1 (.in_1(coil_L), .out_2(hiz_detector_1_out_2));
  nor nor_1 (nor_1_out, hiz_detector_1_out_2, hiz_detector_2_out_2);
  HiZ_Detector hiz_detector_2 (.in_1(coil_R), .out_2(hiz_detector_2_out_2));
  xor xor_1 (xor_1_out, coil_L, coil_R);
  assign controlled_buffer_1_out = nor_1_out ? xor_1_out : 1'bz;  // Controlled_Buffer controlled_buffer_1
  Pull_Resistor pull_resistor_1 (.node(controlled_buffer_1_out));
  D_Flip_Flop d_ff_1 (.D(controlled_buffer_1_out), .clk(CLK), .Q(d_ff_1_q));  // open: Qn, preset, reset
  xnor xnor_1 (xnor_1_out, controlled_buffer_1_out, d_ff_1_q);
  Demultiplexer #(.tristate("true")) demultiplexer_1 (
    .out0(demultiplexer_1_out0), .out1(demultiplexer_1_out1), .in(C1), .sel(controlled_buffer_1_out));
  Demultiplexer #(.tristate("true")) demultiplexer_2 (
    .out0(demultiplexer_2_out0), .out1(demultiplexer_2_out1), .in(C2), .sel(controlled_buffer_1_out));
  assign NC1 = xnor_1_out ? demultiplexer_1_out0 : 1'bz;  // Controlled_Buffer controlled_buffer_2
  assign NO1 = xnor_1_out ? demultiplexer_1_out1 : 1'bz;  // Controlled_Buffer controlled_buffer_3
  assign NC2 = xnor_1_out ? demultiplexer_2_out0 : 1'bz;  // Controlled_Buffer controlled_buffer_4
  assign NO2 = xnor_1_out ? demultiplexer_2_out1 : 1'bz;  // Controlled_Buffer controlled_buffer_5
endmodule

module DPDT_CICO (
  input  C1,
  input  coil_L,
  input  coil_R,
  input  NC2,
  input  CLK,
  input  NO2,
  output NC1,
  output NO1,
  output C2
);

  wire controlled_buffer_1_out, d_ff_1_q, demultiplexer_1_out0, demultiplexer_1_out1, hiz_detector_1_out_2,
       hiz_detector_2_out_2, multiplexer_1_out, nor_1_out, xnor_1_out, xor_1_out;

  HiZ_Detector hiz_detector_1 (.in_1(coil_L), .out_2(hiz_detector_1_out_2));
  nor nor_1 (nor_1_out, hiz_detector_1_out_2, hiz_detector_2_out_2);
  HiZ_Detector hiz_detector_2 (.in_1(coil_R), .out_2(hiz_detector_2_out_2));
  xor xor_1 (xor_1_out, coil_L, coil_R);
  assign controlled_buffer_1_out = nor_1_out ? xor_1_out : 1'bz;  // Controlled_Buffer controlled_buffer_1
  Pull_Resistor pull_resistor_1 (.node(controlled_buffer_1_out));
  D_Flip_Flop d_ff_1 (.D(controlled_buffer_1_out), .clk(CLK), .Q(d_ff_1_q));  // open: Qn, preset, reset
  xnor xnor_1 (xnor_1_out, controlled_buffer_1_out, d_ff_1_q);
  assign C2 = xnor_1_out ? multiplexer_1_out : 1'bz;  // Controlled_Buffer controlled_buffer_2
  Demultiplexer #(.tristate("true")) demultiplexer_1 (
    .out0(demultiplexer_1_out0), .out1(demultiplexer_1_out1), .in(C1), .sel(controlled_buffer_1_out));
  Multiplexer multiplexer_1 (.in0(NC2), .in1(NO2), .out(multiplexer_1_out), .sel(controlled_buffer_1_out));
  assign NC1 = xnor_1_out ? demultiplexer_1_out0 : 1'bz;  // Controlled_Buffer controlled_buffer_3
  assign NO1 = xnor_1_out ? demultiplexer_1_out1 : 1'bz;  // Controlled_Buffer controlled_buffer_4
endmodule

module DPDT_COCI (
  input  NC1,
  input  NO1,
  input  coil_L,
  input  coil_R,
  input  CLK,
  input  C2,
  output C1,
  output NC2,
  output NO2
);

  wire controlled_buffer_1_out, d_ff_1_q, demultiplexer_1_out0, demultiplexer_1_out1, hiz_detector_1_out_2,
       hiz_detector_2_out_2, multiplexer_1_out, nor_1_out, xnor_1_out, xor_1_out;

  HiZ_Detector hiz_detector_1 (.in_1(coil_L), .out_2(hiz_detector_1_out_2));
  nor nor_1 (nor_1_out, hiz_detector_1_out_2, hiz_detector_2_out_2);
  HiZ_Detector hiz_detector_2 (.in_1(coil_R), .out_2(hiz_detector_2_out_2));
  xor xor_1 (xor_1_out, coil_L, coil_R);
  assign controlled_buffer_1_out = nor_1_out ? xor_1_out : 1'bz;  // Controlled_Buffer controlled_buffer_1
  Pull_Resistor pull_resistor_1 (.node(controlled_buffer_1_out));
  D_Flip_Flop d_ff_1 (.D(controlled_buffer_1_out), .clk(CLK), .Q(d_ff_1_q));  // open: Qn, preset, reset
  assign C1 = xnor_1_out ? multiplexer_1_out : 1'bz;  // Controlled_Buffer controlled_buffer_2
  xnor xnor_1 (xnor_1_out, controlled_buffer_1_out, d_ff_1_q);
  Multiplexer multiplexer_1 (.in0(NC1), .in1(NO1), .out(multiplexer_1_out), .sel(controlled_buffer_1_out));
  Demultiplexer #(.tristate("true")) demultiplexer_1 (
    .out0(demultiplexer_1_out0), .out1(demultiplexer_1_out1), .in(C2), .sel(controlled_buffer_1_out));
  assign NC2 = xnor_1_out ? demultiplexer_1_out0 : 1'bz;  // Controlled_Buffer controlled_buffer_3
  assign NO2 = xnor_1_out ? demultiplexer_1_out1 : 1'bz;  // Controlled_Buffer controlled_buffer_4
endmodule

module DPDT_COCO (
  input  NC1,
  input  NO1,
  input  coil_L,
  input  coil_R,
  input  NC2,
  input  CLK,
  input  NO2,
  output C1,
  output C2
);

  wire controlled_buffer_1_out, d_ff_1_q, hiz_detector_1_out_2, hiz_detector_2_out_2, multiplexer_1_out,
       multiplexer_2_out, nor_1_out, xnor_1_out, xor_1_out;

  HiZ_Detector hiz_detector_1 (.in_1(coil_L), .out_2(hiz_detector_1_out_2));
  nor nor_1 (nor_1_out, hiz_detector_1_out_2, hiz_detector_2_out_2);
  HiZ_Detector hiz_detector_2 (.in_1(coil_R), .out_2(hiz_detector_2_out_2));
  xor xor_1 (xor_1_out, coil_L, coil_R);
  assign controlled_buffer_1_out = nor_1_out ? xor_1_out : 1'bz;  // Controlled_Buffer controlled_buffer_1
  Pull_Resistor pull_resistor_1 (.node(controlled_buffer_1_out));
  D_Flip_Flop d_ff_1 (.D(controlled_buffer_1_out), .clk(CLK), .Q(d_ff_1_q));  // open: Qn, preset, reset
  assign C1 = xnor_1_out ? multiplexer_1_out : 1'bz;  // Controlled_Buffer controlled_buffer_2
  xnor xnor_1 (xnor_1_out, controlled_buffer_1_out, d_ff_1_q);
  assign C2 = xnor_1_out ? multiplexer_2_out : 1'bz;  // Controlled_Buffer controlled_buffer_3
  Multiplexer multiplexer_1 (.in0(NC1), .in1(NO1), .out(multiplexer_1_out), .sel(controlled_buffer_1_out));
  Multiplexer multiplexer_2 (.in0(NC2), .in1(NO2), .out(multiplexer_2_out), .sel(controlled_buffer_1_out));
endmodule

module Test (
  input  in_1,
  input  in_2
);

  wire dpdt_cici_1_no1, dpdt_cici_1_no2, dpdt_cico_1_no1, dpdt_coci_1_no2, dpdt_coco_1_c2, spdt_ci_1_no1,
       spdt_co_1_c1;

  SPDT_CI spdt_ci_1 (.coil_L(in_2), .coil_R(1'b0), .CLK(in_1), .C1(1'b1), .NO1(spdt_ci_1_no1));  // open: NC1
  LED led_1 (.in(spdt_ci_1_no1));
  SPDT_CO spdt_co_1 (.coil_L(spdt_ci_1_no1), .coil_R(1'b0), .CLK(in_1), .NO1(1'b1), .C1(spdt_co_1_c1));  // open: NC1
  LED led_2 (.in(spdt_co_1_c1));
  DPDT_CICI dpdt_cici_1 (
    .coil_L(spdt_co_1_c1), .coil_R(1'b0), .CLK(in_1), .C1(1'b1), .C2(1'b1), .NO1(dpdt_cici_1_no1),
    .NO2(dpdt_cici_1_no2));  // open: NC1, NC2
  LED led_3 (.in(dpdt_cici_1_no2));
  DPDT_CICO dpdt_cico_1 (
    .coil_L(dpdt_cici_1_no1), .coil_R(1'b0), .CLK(in_1), .C1(1'b1), .NO1(dpdt_cico_1_no1));  // open: NC2, NO2, C2, NC1
  LED led_4 (.in(dpdt_cico_1_no1));
  DPDT_COCI dpdt_coci_1 (
    .coil_L(dpdt_cico_1_no1), .coil_R(1'b0), .CLK(in_1), .C2(1'b1), .NO2(dpdt_coci_1_no2));  // open: NC1, NO1, C1, NC2
  LED led_5 (.in(dpdt_coci_1_no2));
  DPDT_COCO dpdt_coco_1 (
    .coil_L(dpdt_coci_1_no2), .coil_R(1'b0), .CLK(in_1), .NC2(1'b0), .NO2(1'b1), .C2(dpdt_coco_1_c2));  // open: NC1, NO1, C1
  LED led_6 (.in(dpdt_coco_1_c2));
endmodule
