// Logisim project Clackertron - old copy.circ as structural Verilog: 18 circuits, main circuit main
module main (
  input  A,
  input  B,
  input  nB,
  input  CI,
  output S,
  output CO
);

  wire half_add_1_p4, half_add_1_p5, half_add_3_p5, spdt_ci_2_nc1, spdt_ci_2_no1;

  D_Flip_Flop d_ff_1 ();  // open: D, clk, Q, Qn, preset, reset
  D_Register d_register_1 ();  // open: D, EN, Q, nQ
  SPDT_CI spdt_ci_1 ();  // open: coil_L, coil_R, C1, NC1, NO1
  DPDT_CICI dpdt_cici_1 ();  // open: coil_L, coil_R, C1, C2, NC1, NO1, NC2, NO2
  DPDT_CICO dpdt_cico_1 ();  // open: coil_L, coil_R, C1, NC2, NO2, C2, NC1, NO1
  // Half_Add half_add_1: pin names not known; wires that end beside it: A, B, nB, half_add_1_p4, half_add_1_p5
  SPDT_CI spdt_ci_2 (.coil_L(CI), .coil_R(1'b0), .C1(1'b1), .NC1(spdt_ci_2_nc1), .NO1(spdt_ci_2_no1));
  ADD add_1 ();  // open: CI, A, B, nB, S, CO
  SPDT_CO spdt_co_1 ();  // open: coil_L, coil_R, NC1, NO1, C1
  DPDT_COCI dpdt_coci_1 ();  // open: coil_L, coil_R, C2, NC1, NO1, C1, NC2, NO2
  DPDT_COCO dpdt_coco_1 ();  // open: coil_L, coil_R, NC1, NO1, NC2, NO2, C1, C2
  Half_Add half_add_2 ();  // open: A, B, C, S, nS
  // Half_Add half_add_3: pin names not known; wires that end beside it: half_add_1_p4, spdt_ci_2_no1, spdt_ci_2_nc1, S, half_add_3_p5
  or or_1 (CO, half_add_3_p5, half_add_1_p5);
  Full_Add full_add_1 ();  // open: B, nB, A, CI, S, CO
  MUX mux_1 ();  // open: A, B, S, out_4
  DEMUX demux_1 ();  // open: in_1, S, A, B
  ADD_SUB add_sub_1 ();  // open: A, nA, B, nB, CI, s_SUB, s_ADD, S, CO, OA
  INC inc_1 ();  // open: A, CI, S, nS, CO
  INC_DEC inc_dec_1 ();  // open: CI, D, IE, DEC, OE, S, CO

  // Notes on the sheet:
  //   FA old
endmodule

module SPDT_CI (
  input  C1,
  input  coil_L,
  input  coil_R,
  output NC1,
  output NO1
);

  wire xor_1_out;

  Demultiplexer demultiplexer_1 (.out0(NC1), .out1(NO1), .in(C1), .sel(xor_1_out));
  xor xor_1 (xor_1_out, coil_L, coil_R);
endmodule

module SPDT_CO (
  input  NC1,
  input  NO1,
  input  coil_L,
  input  coil_R,
  output C1
);

  wire xor_1_out;

  Multiplexer multiplexer_1 (.in0(NC1), .in1(NO1), .out(C1), .sel(xor_1_out));
  xor xor_1 (xor_1_out, coil_L, coil_R);
endmodule

module DPDT_CICI (
  input  C1,
  input  coil_L,
  input  coil_R,
  input  C2,
  output NC1,
  output NO1,
  output NC2,
  output NO2
);

  wire xor_1_out;

  Demultiplexer demultiplexer_1 (.out0(NC1), .out1(NO1), .in(C1), .sel(xor_1_out));
  xor xor_1 (xor_1_out, coil_L, coil_R);
  Demultiplexer demultiplexer_2 (.out0(NC2), .out1(NO2), .in(C2), .sel(xor_1_out));
endmodule

module DPDT_CICO (
  input  C1,
  input  coil_L,
  input  coil_R,
  input  NC2,
  input  NO2,
  output NC1,
  output NO1,
  output C2
);

  wire xor_1_out;

  Demultiplexer demultiplexer_1 (.out0(NC1), .out1(NO1), .in(C1), .sel(xor_1_out));
  xor xor_1 (xor_1_out, coil_L, coil_R);
  Multiplexer multiplexer_1 (.in0(NC2), .in1(NO2), .out(C2), .sel(xor_1_out));
endmodule

module DPDT_COCI (
  input  NC1,
  input  NO1,
  input  coil_L,
  input  coil_R,
  input  C2,
  output C1,
  output NC2,
  output NO2
);

  wire xor_1_out;

  Multiplexer multiplexer_1 (.in0(NC1), .in1(NO1), .out(C1), .sel(xor_1_out));
  xor xor_1 (xor_1_out, coil_L, coil_R);
  Demultiplexer demultiplexer_1 (.out0(NC2), .out1(NO2), .in(C2), .sel(xor_1_out));
endmodule

module DPDT_COCO (
  input  NC1,
  input  NO1,
  input  coil_L,
  input  coil_R,
  input  NC2,
  input  NO2,
  output C1,
  output C2
);

  wire xor_1_out;

  Multiplexer multiplexer_1 (.in0(NC1), .in1(NO1), .out(C1), .sel(xor_1_out));
  xor xor_1 (xor_1_out, coil_L, coil_R);
  Multiplexer multiplexer_2 (.in0(NC2), .in1(NO2), .out(C2), .sel(xor_1_out));
endmodule

module D_Register (
  input  [7:0] D,
  input  EN,
  output [7:0] Q,
  output [7:0] nQ
);

  D_Flip_Flop #(.trigger("high")) d_ff_1 (.D(D[0]), .clk(EN), .Q(Q[0]), .Qn(nQ[0]));  // open: preset, reset
  D_Flip_Flop #(.trigger("high")) d_ff_2 (.D(D[1]), .clk(EN), .Q(Q[1]), .Qn(nQ[1]));  // open: preset, reset
  D_Flip_Flop #(.trigger("high")) d_ff_3 (.D(D[2]), .clk(EN), .Q(Q[2]), .Qn(nQ[2]));  // open: preset, reset
  D_Flip_Flop #(.trigger("high")) d_ff_4 (.D(D[3]), .clk(EN), .Q(Q[3]), .Qn(nQ[3]));  // open: preset, reset
  D_Flip_Flop #(.trigger("high")) d_ff_5 (.D(D[4]), .clk(EN), .Q(Q[4]), .Qn(nQ[4]));  // open: preset, reset
  D_Flip_Flop #(.trigger("high")) d_ff_6 (.D(D[5]), .clk(EN), .Q(Q[5]), .Qn(nQ[5]));  // open: preset, reset
  D_Flip_Flop #(.trigger("high")) d_ff_7 (.D(D[6]), .clk(EN), .Q(Q[6]), .Qn(nQ[6]));  // open: preset, reset
  D_Flip_Flop #(.trigger("high")) d_ff_8 (.D(D[7]), .clk(EN), .Q(Q[7]), .Qn(nQ[7]));  // open: preset, reset
endmodule

module Half_Add (
  input  A,
  input  B,
  output S,
  output nS,
  output C
);

  DPDT_CICO dpdt_cico_1 (.coil_L(A), .coil_R(B), .C1(1'b1), .NC2(B), .NO2(1'b0), .C2(C), .NC1(nS), .NO1(S));

  // Notes on the sheet:
  //   Half Adder Relay equivalent
endmodule

module Full_Add (
  input  B,
  input  nB,
  input  A,
  input  CI,
  output S,
  output CO
);

  DPDT_COCO dpdt_coco_1 (.coil_L(CI), .coil_R(A), .NC1(A), .NO1(B), .NC2(B), .NO2(nB), .C1(CO), .C2(S));
endmodule

module ADD (
  input  CI,
  input  [7:0] A,
  input  [7:0] B,
  input  [7:0] nB,
  output [7:0] S,
  output CO
);

  wire full_add_1_co, full_add_2_co, full_add_3_co, full_add_4_co, full_add_5_co, full_add_6_co,
       full_add_7_co;

  Full_Add full_add_1 (.B(B[0]), .nB(nB[0]), .A(A[0]), .CI(CI), .S(S[0]), .CO(full_add_1_co));
  Full_Add full_add_2 (.B(B[1]), .nB(nB[1]), .A(A[1]), .CI(full_add_1_co), .S(S[1]), .CO(full_add_2_co));
  Full_Add full_add_3 (.B(B[2]), .nB(nB[2]), .A(A[2]), .CI(full_add_2_co), .S(S[2]), .CO(full_add_3_co));
  Full_Add full_add_4 (.B(B[3]), .nB(nB[3]), .A(A[3]), .CI(full_add_3_co), .S(S[3]), .CO(full_add_4_co));
  Full_Add full_add_5 (.B(B[4]), .nB(nB[4]), .A(A[4]), .CI(full_add_4_co), .S(S[4]), .CO(full_add_5_co));
  Full_Add full_add_6 (.B(B[5]), .nB(nB[5]), .A(A[5]), .CI(full_add_5_co), .S(S[5]), .CO(full_add_6_co));
  Full_Add full_add_7 (.B(B[6]), .nB(nB[6]), .A(A[6]), .CI(full_add_6_co), .S(S[6]), .CO(full_add_7_co));
  Full_Add full_add_8 (.B(B[7]), .nB(nB[7]), .A(A[7]), .CI(full_add_7_co), .S(S[7]), .CO(CO));
endmodule

module ADD_SUB (
  input  [7:0] A,
  input  [7:0] nA,
  input  [7:0] B,
  input  [7:0] nB,
  input  CI,
  input  s_SUB,
  input  s_ADD,
  output [7:0] S,
  output CO,
  output OA
);

  wire add_1_co;
  wire [7:0] mux_1_out_4;

  MUX mux_1 (.A(A), .B(nA), .S(s_SUB), .out_4(mux_1_out_4));
  ADD add_1 (.CI(CI), .A(mux_1_out_4), .B(B), .nB(nB), .S(S), .CO(add_1_co));
  SPDT_CO spdt_co_1 (.coil_L(add_1_co), .coil_R(1'b0), .NC1(s_SUB), .NO1(s_ADD), .C1(CO));
  or or_1 (OA, s_SUB, s_ADD);

  // Notes on the sheet:
  //   Relay logic invalid for ~SUB & ~ADD
  //   Output Available
endmodule

module MUX (
  input  [7:0] A,
  input  [7:0] B,
  input  S,
  output [7:0] out_4
);

  DPDT_COCO dpdt_coco_1 (
    .coil_L(S), .coil_R(1'b0), .NC1(A[0]), .NO1(B[0]), .NC2(A[1]), .NO2(B[1]), .C1(out_4[0]), .C2(out_4[1]));
  DPDT_COCO dpdt_coco_2 (
    .coil_L(S), .coil_R(1'b0), .NC1(A[2]), .NO1(B[2]), .NC2(A[3]), .NO2(B[3]), .C1(out_4[2]), .C2(out_4[3]));
  DPDT_COCO dpdt_coco_3 (
    .coil_L(S), .coil_R(1'b0), .NC1(A[4]), .NO1(B[4]), .NC2(A[5]), .NO2(B[5]), .C1(out_4[4]), .C2(out_4[5]));
  DPDT_COCO dpdt_coco_4 (
    .coil_L(S), .coil_R(1'b0), .NC1(A[6]), .NO1(B[6]), .NC2(A[7]), .NO2(B[7]), .C1(out_4[6]), .C2(out_4[7]));
endmodule

module DEMUX (
  input  [7:0] in_1,
  input  S,
  output [7:0] A,
  output [7:0] B
);

  DPDT_CICI dpdt_cici_1 (
    .coil_L(S), .coil_R(1'b0), .C1(in_1[0]), .C2(in_1[1]), .NC1(A[0]), .NO1(B[0]), .NC2(A[1]), .NO2(B[1]));
  DPDT_CICI dpdt_cici_2 (
    .coil_L(S), .coil_R(1'b0), .C1(in_1[2]), .C2(in_1[3]), .NC1(A[2]), .NO1(B[2]), .NC2(A[3]), .NO2(B[3]));
  DPDT_CICI dpdt_cici_3 (
    .coil_L(S), .coil_R(1'b0), .C1(in_1[4]), .C2(in_1[5]), .NC1(A[4]), .NO1(B[4]), .NC2(A[5]), .NO2(B[5]));
  DPDT_CICI dpdt_cici_4 (
    .coil_L(S), .coil_R(1'b0), .C1(in_1[6]), .C2(in_1[7]), .NC1(A[6]), .NO1(B[6]), .NC2(A[7]), .NO2(B[7]));
endmodule

module INC (
  input  CI,
  input  [7:0] A,
  output [7:0] S,
  output [7:0] nS,
  output CO
);

  wire half_add_1_c, half_add_2_c, half_add_3_c, half_add_4_c, half_add_5_c, half_add_6_c, or_1_out;

  or or_1 (or_1_out, CI, A[0]);
  SPDT_CI spdt_ci_1 (.coil_L(CI), .coil_R(A[0]), .C1(1'b1), .NC1(S[0]), .NO1(nS[0]));
  Half_Add half_add_1 (.A(or_1_out), .B(A[1]), .C(half_add_1_c), .S(S[1]), .nS(nS[1]));
  Half_Add half_add_2 (.A(half_add_1_c), .B(A[2]), .C(half_add_2_c), .S(S[2]), .nS(nS[2]));
  Half_Add half_add_3 (.A(half_add_2_c), .B(A[3]), .C(half_add_3_c), .S(S[3]), .nS(nS[3]));
  Half_Add half_add_4 (.A(half_add_3_c), .B(A[4]), .C(half_add_4_c), .S(S[4]), .nS(nS[4]));
  Half_Add half_add_5 (.A(half_add_4_c), .B(A[5]), .C(half_add_5_c), .S(S[5]), .nS(nS[5]));
  Half_Add half_add_6 (.A(half_add_5_c), .B(A[6]), .C(half_add_6_c), .S(S[6]), .nS(nS[6]));
  Half_Add half_add_7 (.A(half_add_6_c), .B(A[7]), .C(CO), .S(S[7]), .nS(nS[7]));
endmodule

module INC_DEC (
  input  CI,
  input  [7:0] D,
  input  IE,
  input  DEC,
  input  OE,
  output [7:0] S,
  output CO
);

  wire d_ff_1_q, d_ff_1_qn, inc_1_co, spdt_ci_1_nc1;
  wire [7:0] d_register_1_nq, d_register_1_q, inc_1_ns, inc_1_s, mux_1_out_4, mux_2_out_4;

  D_Flip_Flop #(.trigger("high")) d_ff_1 (.D(CI), .clk(IE), .Q(d_ff_1_q), .Qn(d_ff_1_qn));  // open: preset, reset
  D_Register d_register_1 (.D(D), .EN(IE), .Q(d_register_1_q), .nQ(d_register_1_nq));
  // NoConnect on d_ff_1_qn
  MUX mux_1 (.A(d_register_1_q), .B(d_register_1_nq), .S(DEC), .out_4(mux_1_out_4));
  INC inc_1 (.A(mux_1_out_4), .CI(d_ff_1_q), .S(inc_1_s), .nS(inc_1_ns), .CO(inc_1_co));
  MUX mux_2 (.A(inc_1_s), .B(inc_1_ns), .S(DEC), .out_4(mux_2_out_4));
  SPDT_CI spdt_ci_1 (.coil_L(1'b0), .coil_R(OE), .C1(inc_1_co), .NC1(spdt_ci_1_nc1), .NO1(CO));
  MUX mux_3 (.B(mux_2_out_4), .S(OE), .out_4(S));  // open: A
  // NoConnect on spdt_ci_1_nc1

  // Notes on the sheet:
  //   output must not feedback input
endmodule

module LU (
  input  [7:0] A,
  input  [7:0] nA,
  input  [7:0] B,
  input  [7:0] nB,
  input  s_A,
  input  s_OR,
  input  s_XOR,
  input  s_AND,
  input  s_NEG,
  input  CI,
  input  s_ROR,
  input  s_ROL,
  input  s_LSR,
  input  s_ASL
);
endmodule

module PC (
  input  CI,
  input  [7:0] D_BUS_I,
  input  [7:0] S_BUS_I,
  input  [7:0] AD_BUS_I,
  output [7:0] D_BUS_O,
  output [7:0] S_BUS_O,
  output [7:0] AD_BUS_O,
  output CO
);

  MUX mux_1 ();  // open: A, B, S, out_4
  D_Register d_register_1 ();  // open: D, EN, Q, nQ
endmodule
