// Logisim project Relay_async.circ as structural Verilog: 6 circuits, main circuit SPDT_CI
module SPDT_CI (
  input  C1,
  input  coil_L,
  input  coil_R,
  output NC1,
  output NO1
);

  wire xor_1_out;

  Demultiplexer demultiplexer_1 (.out0(NC1), .out1(NO1), .in(C1), .sel(xor_1_out));
  xor xor_1 (xor_1_out, coil_L, coil_R);
endmodule

module SPDT_CO (
  input  NC1,
  input  NO1,
  input  coil_L,
  input  coil_R,
  output C1
);

  wire xor_1_out;

  Multiplexer multiplexer_1 (.in0(NC1), .in1(NO1), .out(C1), .sel(xor_1_out));
  xor xor_1 (xor_1_out, coil_L, coil_R);
endmodule

module DPDT_CICI (
  input  C1,
  input  coil_L,
  input  coil_R,
  input  C2,
  output NC1,
  output NO1,
  output NC2,
  output NO2
);

  wire xor_1_out;

  Demultiplexer demultiplexer_1 (.out0(NC1), .out1(NO1), .in(C1), .sel(xor_1_out));
  xor xor_1 (xor_1_out, coil_L, coil_R);
  Demultiplexer demultiplexer_2 (.out0(NC2), .out1(NO2), .in(C2), .sel(xor_1_out));
endmodule

module DPDT_CICO (
  input  C1,
  input  coil_L,
  input  coil_R,
  input  NC2,
  input  NO2,
  output NC1,
  output NO1,
  output C2
);

  wire xor_1_out;

  Demultiplexer demultiplexer_1 (.out0(NC1), .out1(NO1), .in(C1), .sel(xor_1_out));
  xor xor_1 (xor_1_out, coil_L, coil_R);
  Multiplexer multiplexer_1 (.in0(NC2), .in1(NO2), .out(C2), .sel(xor_1_out));
endmodule

module DPDT_COCI (
  input  NC1,
  input  NO1,
  input  coil_L,
  input  coil_R,
  input  C2,
  output C1,
  output NC2,
  output NO2
);

  wire xor_1_out;

  Multiplexer multiplexer_1 (.in0(NC1), .in1(NO1), .out(C1), .sel(xor_1_out));
  xor xor_1 (xor_1_out, coil_L, coil_R);
  Demultiplexer demultiplexer_1 (.out0(NC2), .out1(NO2), .in(C2), .sel(xor_1_out));
endmodule

module DPDT_COCO (
  input  NC1,
  input  NO1,
  input  coil_L,
  input  coil_R,
  input  NC2,
  input  NO2,
  output C1,
  output C2
);

  wire xor_1_out;

  Multiplexer multiplexer_1 (.in0(NC1), .in1(NO1), .out(C1), .sel(xor_1_out));
  xor xor_1 (xor_1_out, coil_L, coil_R);
  Multiplexer multiplexer_2 (.in0(NC2), .in1(NO2), .out(C2), .sel(xor_1_out));
endmodule
